// Logisim project NANDGATE.circ as structural Verilog: 1 circuit, main circuit main
module main (
  input  B,
  input  C,
  input  in_3
);

  wire controlled_inverter_1_out, controlled_inverter_2_out, controlled_inverter_3_out, nand_1_out,
       nand_2_out, nand_3_out, nand_4_out, nand_5_out, undriven, undriven_2, undriven_3;

  Controlled_Inverter controlled_inverter_1 (.in(undriven), .out(controlled_inverter_1_out));  // open: en
  Controlled_Inverter controlled_inverter_2 (.in(undriven_2), .out(controlled_inverter_2_out));  // open: en
  Controlled_Inverter controlled_inverter_3 (.in(undriven_3), .out(controlled_inverter_3_out));  // open: en
  nand nand_1 (nand_1_out, undriven, undriven_2, undriven_3);
  nand nand_2 (nand_2_out, controlled_inverter_1_out, undriven_2, undriven_3);
  nand nand_3 (nand_3_out, undriven, controlled_inverter_2_out, controlled_inverter_3_out);
  nand nand_4 (nand_4_out, undriven, controlled_inverter_2_out, undriven_3);
  nand nand_5 (nand_5_out, controlled_inverter_1_out, controlled_inverter_2_out, undriven_3);
  // NAND_Gate nand_6 has open pins: in0=nand_1_out, in1=nand_2_out, in2=nand_3_out, in3=nand_4_out, in4=nand_5_out, out=open

  // Notes on the sheet:
  //   A
endmodule
