// Logisim project andorgate.circ as structural Verilog: 1 circuit, main circuit main
module main (
  input  A,
  input  B,
  input  C
);

  wire and_1_out, and_2_out, and_3_out, and_4_out, and_5_out, not_1_out, not_2_out, not_3_out, undriven,
       undriven_2, undriven_3;

  not not_1 (not_1_out, undriven);
  not not_2 (not_2_out, undriven_3);
  not not_3 (not_3_out, undriven_2);
  and and_1 (and_1_out, undriven, undriven_2, undriven_3);
  and and_2 (and_2_out, not_1_out, undriven_2, undriven_3);
  and and_3 (and_3_out, undriven, not_3_out, not_2_out);
  and and_4 (and_4_out, undriven, not_3_out, undriven_3);
  and and_5 (and_5_out, not_1_out, not_3_out, undriven_3);
  // OR_Gate or_1 has open pins: in0=and_1_out, in1=and_2_out, in2=and_3_out, in3=and_4_out, in4=and_5_out, out=open
endmodule
